# Fritzing sketch Trabalho_Robotica (saved by Fritzing 0.8.7b)
breadboards: 1

parts:
  DHT1 = DHT11 Humitidy and Temperature Sensor
  LED2 = RGB LED (com. cathode, rbg) [package="5 mm [THT]"]
  R1 = Resistor [package="2512 [SMD]"]
  Componente1 = Arduino Uno (Rev3)
  R2 = Resistor [package="2512 [SMD]"]
  R3 = Resistor [package="2512 [SMD]"]
  VCC1 = 4 x AAA Battery Mount
  U1 = RELAY [package=relay-jzc]
  Power_plug1 = Power plug

nets:
  VDD: DHT1.VDD, LED2.common_cathode, Componente1.5V
  N1: DHT1.DATA, Componente1.D3_PWM
  GND: DHT1.GND, Componente1.GND, VCC1.-, U1.MAIN
  N2: LED2.red_anode, R2.Pin_0
  N3: LED2.blue_anode, R3.Pin_0
  N4: LED2.green_anode, R1.Pin_0
  N5: R1.Pin_1, Componente1.D6_PWM
  N6: Componente1.D8, R2.Pin_1
  N7: Componente1.AREF, VCC1.+
  N8: Componente1.D2, U1.COIL1
  N9: Componente1.D7, R3.Pin_1
  N10: U1.COIL2, Power_plug1.VCC

notes:
  110 / 220 VAC

custom parts:
  DHT11 Humitidy and Temperature Sensor: DHT11 Humidity and Temperature Sensor
